# Fritzing sketch tonuino (saved by Fritzing 0.9.4)
perfboards: 2

parts:
  R1 = Resistor [tolerance=±5% resistance=10k package=THT]
  C1 = Ceramic Capacitor [capacitance=100nF package="100 mil [THT, multilayer]"]
  Power_plug1 = Power plug
  J7 = shrouded pin header, 12 pins [form="♂ (shrouded male)"]
  C2 = Ceramic Capacitor [capacitance=100nF package="100 mil [THT, multilayer]"]
  J1 = male pin header, 9 pins [form="♂ (male)"]
  J8 = male pin header, 9 pins [form="♂ (male)"]
  J5 = male pin header, 9 pins [form="♂ (male)"]
  J4 = male pin header, 9 pins [form="♂ (male)"]
  J9 = male pin header, 2 pins [form="♂ (male)"]
  J10 = male pin header, 2 pins [form="♂ (male)"]
  23LCV1 = 23LCV1024 [part_number=23LCV1024 package="DIP (Dual Inline) [THT]"]
  J11 = male pin header, 7 pins [form="♂ (male)"]
  SP1 = SPEAKER [package=pcb_mount_speaker]  # not connected
  RFID = male pin header, 8 pins [form="♂ (male)"]
  RFID1 = male pin header, 3 pins [form="♂ (male)"]
  RFID2 = male pin header, 4 pins [form="♂ (male)"]
  RFID3 = male pin header, 1 pin [form="♂ (male)"]
  R3 = Resistor [tolerance=±5% resistance=100k package=THT]
  WeMos_D1_Mini_Battery_Shield1 = WeMos D1 Mini Battery Shield
  U1 = Voltage Regulator - 5V [package="TO220 [THT]"]
  U2 = SWITCH-SPST-2 [package=switch-spst-vertical]
  U3 = LIPO-1000mAh [package=lipo-1000]

nets:
  N1: R1.Pin_0, C1.1, J7.pin12, J4.pin8
  N2: R1.Pin_1, C2.1, J5.pin9, J10.pin1, 23LCV1.NC, RFID.pin8
  N3: C1.0, J7.pin6, C2.0, J4.pin9, RFID.pin6, RFID1.pin3, RFID2.pin4
  N4: Power_plug1.VCC, U1.input_voltage
  GND: Power_plug1.GND, U1.GND
  N5: J7.pin1, J4.pin2
  N6: J7.pin4, J5.pin7
  N7: J7.pin5, J5.pin8
  N8: J1.pin4, RFID.pin3
  N9: J1.pin5, RFID.pin2
  N10: J1.pin6, J11.pin2
  N11: J1.pin7, RFID3.pin1, R3.Pin_0, WeMos_D1_Mini_Battery_Shield1.A0
  N12: J8.pin4, RFID.pin4
  N13: J8.pin5, RFID2.pin2
  N14: J8.pin6, J11.pin1
  N15: J5.pin1, RFID1.pin2
  N16: J5.pin2, RFID1.pin1
  N17: J5.pin3, RFID2.pin3
  N18: J5.pin4, 23LCV1.SCK
  N19: J5.pin5, RFID2.pin1
  N20: J4.pin1, RFID.pin1
  N21: J4.pin3, RFID.pin7
  N22: J4.pin4, 23LCV1.CS_
  N23: J4.pin5, 23LCV1.SO/SIO1
  N24: J4.pin6, J11.pin3
  N25: J4.pin7, 23LCV1.SI/SIO0
  N26: J9.pin1, J11.pin7, WeMos_D1_Mini_Battery_Shield1.5V
  N27: J9.pin2, J11.pin6, WeMos_D1_Mini_Battery_Shield1.G
  N28: J10.pin2, 23LCV1.VSS, R3.Pin_1
  N29: U2.P, U3.-

notes:
  toniebox PSU 9V
  Voltage regulator
